# Fritzing sketch schematic (saved by Fritzing 1.0.3b)
breadboards: 1

parts:
  Arduino_D1_(Wemos)_D1_R1 = Arduino Uno (Rev3) - ICSP
  V1 = DC Power [voltage=5V internal_resistance=0.1Ω]
  CD74HC4067 = Analog Digital MUX Breakout
  BS_1 = Pushbutton [package=THT]
  BS_2 = Pushbutton [package=THT]
  BS_3 = Pushbutton [package=THT]
  BS_4 = Pushbutton [package=THT]
  BS_5 = Pushbutton [package=THT]
  BS_6 = Pushbutton [package=THT]
  BS_7 = Pushbutton [package=THT]
  BS_8 = Pushbutton [package=THT]
  BS_9 = Pushbutton [package=THT]
  Crane_Rotator = Basic Servo
  Crane_Up/Down = Basic Servo
  Crane_Extender?? = Basic Servo
  Electromagnet = Inductor [package="400 mil [THT]"]

nets:
  N1: Arduino_D1_(Wemos)_D1_R1.A0, CD74HC4067.SIG
  GND: Arduino_D1_(Wemos)_D1_R1.GND, V1.V-, CD74HC4067.GND, CD74HC4067.EN, Crane_Rotator.gnd, Crane_Up/Down.gnd, Crane_Extender??.gnd, Electromagnet.pin_0
  N2: Arduino_D1_(Wemos)_D1_R1.D8, CD74HC4067.S0
  N3: Arduino_D1_(Wemos)_D1_R1.D9_PWM, CD74HC4067.S1
  N4: Arduino_D1_(Wemos)_D1_R1.D10_PWM/SS, CD74HC4067.S2
  N5: Arduino_D1_(Wemos)_D1_R1.D11_PWM/MOSI, CD74HC4067.S3
  N6: Arduino_D1_(Wemos)_D1_R1.D0/RX, Electromagnet.pin_1
  N7: Arduino_D1_(Wemos)_D1_R1.D2, Crane_Rotator.pulse
  N8: Arduino_D1_(Wemos)_D1_R1.D3_PWM, Crane_Up/Down.pulse
  N9: Arduino_D1_(Wemos)_D1_R1.D4, Crane_Extender??.pulse
  5V: V1.V+, CD74HC4067.VCC, BS_1.leg1, BS_2.leg1, BS_3.leg1, BS_4.leg1, BS_5.leg1, BS_6.leg1, BS_7.leg1, BS_8.leg1, BS_9.leg1, Crane_Rotator.vcc, Crane_Up/Down.vcc, Crane_Extender??.vcc
  N10: CD74HC4067.C0, BS_1.leg0
  N11: CD74HC4067.C1, BS_2.leg0
  N12: CD74HC4067.C2, BS_3.leg0
  N13: CD74HC4067.C3, BS_4.leg0
  N14: CD74HC4067.C4, BS_5.leg0
  N15: CD74HC4067.C5, BS_6.leg0
  N16: CD74HC4067.C6, BS_7.leg0
  N17: CD74HC4067.C7, BS_8.leg0
  N18: CD74HC4067.C8, BS_9.leg0

notes:
  BS = Board square
  We do not use push buttons. They represent a game piece being placed or not. The "switch" will be on with varying resistors
